// Logisim project GeneradorPixeles.circ as structural Verilog: 1 circuit, main circuit GeneradorPixeles
module GeneradorPixeles (
  input  Clock,
  output [3:0] Y,
  output [3:0] X
);

  wire contadorx_1_carry;

  contadorX contadorx_1 (.Reset(Clock), .Carry(contadorx_1_carry), .X(X));  // open: Start, Clock
  contadorY contadory_1 (.Clock(contadorx_1_carry), .Y(Y));
endmodule
