// Logisim project intentodeCalculoF.circ as structural Verilog: 1 circuit, main circuit main
module main (
  input  [3:0] A,
  input  [3:0] B,
  input  [3:0] C,
  input  Clock,
  input  [3:0] Y,
  input  Reset,
  input  Start
);

  wire [15:0] F_in, F_out, F_row_in, F_row_out;

  CarrySkipAdder carryskipadder_1 (.A(F_out), .B({{13{A[3]}}, A[2:0]}), .S(F_in));  // open: C_in, C_out
  CarrySkipAdder carryskipadder_2 (.A(F_row_out), .B({{13{B[3]}}, B[2:0]}), .S(F_row_in));  // open: C_in, C_out
  Register #(.width(16)) F (.D(F_in), .clk(Clock), .Q(F_out), .clr(Reset));  // open: en
  Register #(.width(16)) F_row (.clk(Clock), .Q(F_row_out), .clr(Reset));  // open: D, en
endmodule
